# Fritzing sketch Schematic (saved by Fritzing 1.0.4)
breadboards: 1
stripboards: 1

parts:
  Pololu_A1 = Pololu A4988 [package=SO16]
  M1 = Stepper Motor - Bipolar
  Nano1 = Arduino Nano v2.3
  C1 = Electrolytic Capacitor [capacitance=100µF voltage=35V package="1010 [SMD, electrolytic]"]
  TRM1 = Terminal 2pin
  Pololu_A2 = Pololu A4988 [package=SO16]
  M2 = Stepper Motor - Bipolar
  Nano2 = Arduino Nano v2.3
  C2 = Electrolytic Capacitor [capacitance=100µF voltage=35V package="1010 [SMD, electrolytic]"]
  TRM2 = Terminal 2pin

nets:
  N1: Pololu_A1.MS1, Nano1.D6
  N2: Pololu_A1.MS2, Nano1.D5
  N3: Pololu_A1.MS3, Nano1.D4
  N4: Pololu_A1.RESET, Pololu_A1.SLEEP
  N5: Pololu_A1.STEP, Nano1.D3
  N6: Pololu_A1.DIR, Nano1.D2
  N7: Pololu_A1.GND#8, Nano1.GND
  VDD: Pololu_A1.VDD, Nano1.+5V
  N8: Pololu_A1.1B, M1.D
  N9: Pololu_A1.1A, M1.B
  N10: Pololu_A1.2A, M1.C
  N11: Pololu_A1.2B, M1.A
  N12: Pololu_A1.GND#14, C1.-, TRM1.pin_1
  N13: Pololu_A1.VMOT, C1.+, TRM1.pin_2
  N14: Pololu_A2.MS1, Nano2.D6
  N15: Pololu_A2.MS2, Nano2.D5
  N16: Pololu_A2.MS3, Nano2.D4
  N17: Pololu_A2.RESET, Pololu_A2.SLEEP
  N18: Pololu_A2.STEP, Nano2.D3
  N19: Pololu_A2.DIR, Nano2.D2
  N20: Pololu_A2.GND#8, Nano2.GND
  VDD_2: Pololu_A2.VDD, Nano2.+5V
  N21: Pololu_A2.1B, M2.D
  N22: Pololu_A2.1A, M2.B
  N23: Pololu_A2.2A, M2.C
  N24: Pololu_A2.2B, M2.A
  N25: Pololu_A2.GND#14, C2.-, TRM2.pin_1
  N26: Pololu_A2.VMOT, C2.+, TRM2.pin_2

custom parts:
  Terminal 2pin: 2-pin Terminal Block
